// Digital circuit ALU.dig as structural Verilog
module ALU (
  input  [7:0] N,
  input  EN,
  input  Clk,
  input  [2:0] Op,
  output [7:0] AC,
  output [7:0] MQ
);

  wire [7:0] LEFT, MULT_HIGH, MULT_LOW, multiplexer_1_out, multiplexer_2_out, NAND, Q, R, RIGHT, SUB, SUM,
       XOR;

  Add #(.Bits(8)) add_1 (.a(AC), .b(N), .c_i(1'b0), .s(SUM));  // open: c_o
  Sub #(.Bits(8)) sub_1 (.a(AC), .b(N), .c_i(1'b0), .s(SUB));  // open: c_o
  Mul #(.Bits(8)) mul_1 (.a(AC), .b(N), .mul({MULT_LOW, MULT_HIGH}));
  Div #(.Bits(8)) div_1 (.a(AC), .b(N), .q(Q), .r(R));
  BarrelShifter #(.Bits(8)) barrelshifter_1 (.in(AC), .shift(4'b0001), .out(LEFT));
  BarrelShifter #(.Bits(8)) barrelshifter_2 (.in(AC), .shift(4'b0001), .out(RIGHT));
  assign NAND = ~(AC & N);  // NAnd nand_1, 8 bits wide
  assign XOR = AC ^ N;  // XOr xor_1, 8 bits wide
  Multiplexer #(.Selector_Bits(3), .Bits(8)) multiplexer_1 (
    .sel(Op), .in_0(SUM), .in_1(SUB), .in_2(MULT_LOW), .in_3(R), .in_4(NAND), .in_5(XOR), .in_6(LEFT),
    .in_7(RIGHT), .out(multiplexer_1_out));
  Multiplexer #(.Selector_Bits(3), .Bits(8)) multiplexer_2 (
    .sel(Op), .in_0(MQ), .in_1(MQ), .in_2(MULT_HIGH), .in_3(Q), .in_4(MQ), .in_5(MQ), .in_6(MQ), .in_7(MQ),
    .out(multiplexer_2_out));
  Register #(.Bits(8)) register_1 (.D(multiplexer_2_out), .C(Clk), .en(EN), .Q(MQ));
  Register #(.Bits(8)) register_2 (.D(multiplexer_1_out), .C(Clk), .en(EN), .Q(AC));
endmodule
