// Digital circuit PC.dig as structural Verilog
module PC (
  input  CLK,
  input  EN,
  output [7:0] ADDR
);

  wire G3;
  wire [7:0] add_1_s;

  Register #(.Bits(8)) register_1 (.D(add_1_s), .C(CLK), .en(EN), .Q(ADDR));
  Add #(.Bits(8)) add_1 (.a(ADDR), .b(8'h1), .c_i(1'b0), .s(add_1_s), .c_o(G3));
endmodule
