// Digital circuit cpu.dig as structural Verilog
module cpu (
  input  CLK,
  output [7:0] Ac,
  output [7:0] Mq
);

  wire DQ, Q;
  wire [1:0] pc_1_p3;
  wire [2:0] OpC;
  wire [7:0] N, rom_1_d;

  D_FF d_ff_1 (.D(Q), .C(CLK), .Q(DQ), .nQ(Q));
  // PC pc_1: pin names not known; wires that end beside it: CLK, DQ, pc_1_p3
  ALU alu_1 (.N(N), .EN(DQ), .Clk(CLK), .Op(OpC), .AC(Ac), .MQ(Mq));
  ROM #(.Bits(8)) rom_1 (.A(pc_1_p3), .sel(Q), .D(rom_1_d));
  Register #(.Bits(8)) register_1 (.D(rom_1_d), .C(CLK), .en(Q), .Q(N));
  // Pins of 8 and 11 bits meet at {OpC, N}
endmodule
